# Fritzing sketch ir-photon (saved by Fritzing 0.9.2b)
breadboards: 1

parts:
  Part1 = Photon
  VCC1 = 4 x AAA Battery Mount
  R1 = Resistor [tolerance=±5% resistance=1k package="2010 [SMD]"]
  R2 = Resistor [tolerance=±5% resistance=1k package="2010 [SMD]"]
  J1 = Infrared Proximity Sensor
  C1 = Electrolytic Capacitor [capacitance=10µF package="100 mil [THT, electrolytic]"]
  D1 = Rectifier Diode [package="Melf DO-213 AA [SMD]"]
  S1 = Pushbutton [package=THT]

nets:
  N1: Part1.A2, D1.cathode
  GND: Part1.GND, VCC1.-, R2.Pin_1, J1.GND, C1.-, S1.leg0
  VIN: Part1.VIN, VCC1.+, J1.Vcc, C1.+
  N2: Part1.RST, S1.leg1
  N3: R1.Pin_0, J1.Vout
  N4: R1.Pin_1, R2.Pin_0, D1.anode

notes:
  <- Sharp 2Y0A02 with a 10uf capacitor for smoothing out the signal. As suggested he se https://github.com/FH-Potsdam/Knowledge-Exchange/blob/master/Sharp-Infrared-Sensor/2015-01-29_Sharp_Distance_Exchange_Final.pdf
  Diode on the analog pin for superstition. :-)
  external ower supply with 5V 600mA
  voltage devider as suggested here https://community.particle.io/t/gp2y0a41sk0f-sharp-distance-measuring-sensor/5303/8
