# Fritzing sketch speaker-control (saved by Fritzing 0.8.7b)
breadboards: 1

parts:
  Part1 = Arduino Uno (Rev3)
  U1 = Optocoupler [package=THT]
  R1 = Resistor [tolerance=±5% resistance=220 package=THT]
  SP1 = SPEAKER [package=pcb_mount_speaker]
  VCC1 = Battery

nets:
  N1: Part1.D12/MISO, R1.Pin_0
  N2: Part1.GND, U1.Pin_2
  N3: U1.Pin_1, R1.Pin_1
  N4: U1.Pin_4, VCC1.-
  N5: U1.Pin_5, SP1.+
  N6: SP1.-, VCC1.+
